// Logisim project logisim_project.circ as structural Verilog: 4 circuits, main circuit main
module main (
);

  wire CLOCK_out, decoder_1_alu_a_register_write, decoder_1_alu_b_register_write,
       decoder_1_alu_operation_register_write, decoder_1_alu_result_register_write, decoder_1_data_switch,
       decoder_1_program_address_register_a_write, decoder_1_program_address_register_b_write,
       decoder_1_program_address_register_c_write, decoder_1_program_address_register_d_write,
       decoder_1_program_address_register_e_write, decoder_1_program_counter_bus_i_toggle,
       decoder_1_program_counter_bus_ii_toggle, decoder_1_program_counter_write,
       decoder_1_ram_address_register_write, decoder_1_rom_data_register_write, decoder_1_select_ram,
       decoder_1_toggle_alu_result_bus_connection, decoder_1_toggle_ram_write_read,
       decoder_1_toggle_rom_data_bus_connection, n4bit_alu_1_carry, n4bit_alu_1_zero, not_1_out, not_2_out,
       not_3_out, or_1_out, t_ff_1_q, t_ff_2_q, t_ff_3_q;
  wire [3:0] ALU_A_q, ALU_B_q, ALU_OP_q, controlled_buffer_1_out, demultiplexer_1_out0, demultiplexer_1_out1,
       n4bit_alu_1_result, PROGRAM_ADDRESS_A_q, PROGRAM_ADDRESS_B_q, PROGRAM_ADDRESS_C_q, RAM_ADDRESS_q,
       RESULT_q, rom_1_data, rom_1_data_2, ROM_DATA_q;
  wire [11:0] controlled_buffer_2_out, PROGRAM_ADDRESS_E_II_q, PROGRAM_COUNTER_q;

  Hex_Digit_Display hex_digit_display_1 (.value(controlled_buffer_1_out));  // open: dp
  Clock CLOCK (.out(CLOCK_out));
  Register #(.width(4)) PROGRAM_ADDRESS_A (
    .D(controlled_buffer_1_out), .en(decoder_1_program_address_register_a_write), .Q(PROGRAM_ADDRESS_A_q),
    .clk(not_2_out));  // open: clr
  Register #(.width(4)) PROGRAM_ADDRESS_B (
    .D(controlled_buffer_1_out), .en(decoder_1_program_address_register_b_write), .Q(PROGRAM_ADDRESS_B_q),
    .clk(not_2_out));  // open: clr
  Register #(.width(4)) PROGRAM_ADDRESS_C (
    .D(controlled_buffer_1_out), .en(decoder_1_program_address_register_c_write), .Q(PROGRAM_ADDRESS_C_q),
    .clk(not_2_out));  // open: clr
  not not_1 (not_1_out, CLOCK_out);
  Register #(.width(4)) ROM_DATA (
    .D(demultiplexer_1_out1), .en(decoder_1_rom_data_register_write), .Q(ROM_DATA_q), .clk(not_2_out));  // open: clr
  Register #(.width(4)) ALU_OP (
    .D(controlled_buffer_1_out), .en(decoder_1_alu_operation_register_write), .Q(ALU_OP_q), .clk(not_2_out));  // open: clr
  Register #(.width(4)) ALU_A (
    .D(controlled_buffer_1_out), .en(decoder_1_alu_a_register_write), .Q(ALU_A_q), .clk(not_2_out));  // open: clr
  Register #(.width(4)) ALU_B (
    .D(controlled_buffer_1_out), .en(decoder_1_alu_b_register_write), .Q(ALU_B_q), .clk(not_2_out));  // open: clr
  Register #(.width(4)) RAM_ADDRESS (
    .D(controlled_buffer_1_out), .en(decoder_1_ram_address_register_write), .Q(RAM_ADDRESS_q), .clk(not_2_out));  // open: clr
  not not_2 (not_2_out, not_1_out);
  assign controlled_buffer_1_out = t_ff_1_q ? ROM_DATA_q : 4'bz;  // Controlled_Buffer controlled_buffer_1
  T_Flip_Flop t_ff_1 (
    .clk(not_2_out), .T(decoder_1_toggle_rom_data_bus_connection), .Q(t_ff_1_q));  // open: Qn, preset, reset, en
  _4bit_ALU u_4bit_alu_1 (
    .A(ALU_A_q), .B(ALU_B_q), .Result(n4bit_alu_1_result), .Op(ALU_OP_q), .Zero(n4bit_alu_1_zero),
    .Carry(n4bit_alu_1_carry));
  assign controlled_buffer_2_out = decoder_1_program_counter_bus_i_toggle ? {PROGRAM_ADDRESS_C_q, PROGRAM_ADDRESS_B_q, PROGRAM_ADDRESS_A_q} : 12'bz;  // Controlled_Buffer controlled_buffer_2
  Register #(.width(4)) RESULT (
    .D(n4bit_alu_1_result), .en(decoder_1_alu_result_register_write), .Q(RESULT_q), .clk(not_2_out));  // open: clr
  RAM #(.addrWidth(4), .dataWidth(4)) ram_1 (
    .addr(RAM_ADDRESS_q), .data(controlled_buffer_1_out), .sel(or_1_out), .clk(not_2_out), .ld(t_ff_2_q));  // open: clr
  or or_1 (or_1_out, decoder_1_select_ram, t_ff_2_q);
  T_Flip_Flop t_ff_2 (
    .clk(not_2_out), .T(decoder_1_toggle_ram_write_read), .Q(t_ff_2_q));  // open: Qn, preset, reset, en
  Counter #(.width(12), .max('hfff)) PROGRAM_COUNTER (
    .load(decoder_1_program_counter_write), .D(controlled_buffer_2_out), .count(not_3_out),
    .Q(PROGRAM_COUNTER_q), .clk(not_1_out));  // open: carry, clr
  not not_3 (not_3_out, decoder_1_program_counter_write);
  assign controlled_buffer_2_out = decoder_1_program_counter_bus_ii_toggle ? PROGRAM_ADDRESS_E_II_q : 12'bz;  // Controlled_Buffer controlled_buffer_3
  assign controlled_buffer_1_out = t_ff_3_q ? RESULT_q : 4'bz;  // Controlled_Buffer controlled_buffer_4
  T_Flip_Flop t_ff_3 (
    .clk(not_2_out), .T(decoder_1_toggle_alu_result_bus_connection), .Q(t_ff_3_q));  // open: Qn, preset, reset, en
  Register #(.width(4)) PROGRAM_ADDRESS_E_I (
    .D(rom_1_data_2), .en(decoder_1_program_address_register_e_write), .Q(PROGRAM_ADDRESS_E_II_q[7:4]),
    .clk(not_2_out));  // open: clr
  Register #(.width(4)) PROGRAM_ADDRESS_E_II (
    .D(rom_1_data), .en(decoder_1_program_address_register_e_write), .Q(PROGRAM_ADDRESS_E_II_q[3:0]),
    .clk(not_2_out));  // open: clr
  Register #(.width(4)) PROGRAM_ADDRESS_D (
    .D(rom_1_data), .en(decoder_1_program_address_register_d_write), .Q(PROGRAM_ADDRESS_E_II_q[11:8]),
    .clk(not_2_out));  // open: clr
  DECODER decoder_1 (
    .PROGRAM_COUNTER_WRITE(decoder_1_program_counter_write),
    .PROGRAM_ADDRESS_REGISTER_C_WRITE(decoder_1_program_address_register_c_write),
    .PROGRAM_ADDRESS_REGISTER_B_WRITE(decoder_1_program_address_register_b_write),
    .PROGRAM_ADDRESS_REGISTER_A_WRITE(decoder_1_program_address_register_a_write),
    .ROM_DATA_REGISTER_WRITE(decoder_1_rom_data_register_write),
    .ALU_B_REGISTER_WRITE(decoder_1_alu_b_register_write),
    .ALU_A_REGISTER_WRITE(decoder_1_alu_a_register_write),
    .ALU_OPERATION_REGISTER_WRITE(decoder_1_alu_operation_register_write),
    .ALU_RESULT_REGISTER_WRITE(decoder_1_alu_result_register_write),
    .RAM_ADDRESS_REGISTER_WRITE(decoder_1_ram_address_register_write), .SELECT_RAM(decoder_1_select_ram),
    .TOGGLE_RAM_WRITE_READ(decoder_1_toggle_ram_write_read),
    .TOGGLE_ROM_DATA_BUS_CONNECTION(decoder_1_toggle_rom_data_bus_connection),
    .TOGGLE_ALU_RESULT_BUS_CONNECTION(decoder_1_toggle_alu_result_bus_connection),
    .INSTRUCTION(rom_1_data_2), .DATA_SWITCH(decoder_1_data_switch), .DATA(demultiplexer_1_out0),
    .ZERO_FLAG(n4bit_alu_1_zero), .CARRY_FLAG(n4bit_alu_1_carry),
    .PROGRAM_COUNTER_BUS_I_TOGGLE(decoder_1_program_counter_bus_i_toggle), .I_P_CLOCK(not_1_out),
    .PROGRAM_ADDRESS_REGISTER_D_WRITE(decoder_1_program_address_register_d_write),
    .PROGRAM_COUNTER_BUS_II_TOGGLE(decoder_1_program_counter_bus_ii_toggle), .II_P_CLOCK(not_2_out),
    .PROGRAM_ADDRESS_REGISTER_E_WRITE(decoder_1_program_address_register_e_write));
  Hex_Digit_Display hex_digit_display_2 (.value(rom_1_data));  // open: dp
  Hex_Digit_Display hex_digit_display_3 (.value(rom_1_data_2));  // open: dp
  Demultiplexer #(.width(4), .disabled(0), .enable("false")) demultiplexer_1 (
    .out0(demultiplexer_1_out0), .out1(demultiplexer_1_out1), .in(rom_1_data), .sel(decoder_1_data_switch));
  ROM #(.addrWidth(12)) rom_1 (.addr(PROGRAM_COUNTER_q), .data({rom_1_data_2, rom_1_data}), .sel(1'b1));

  // Notes on the sheet:
  //   DATA ON BUS
  //   II P CLOCK
  //   I P CLOCK
  //   INSTRUCTION DATA
  //   contents of rom_1 (hex, n*v repeats v):
  //   10 35 13 31 28 32 13 32 28 31 13 33 28 33 13 34 28 34 13 3f 28 34 13 3f 28 26 31 25 10 12 13 24 12
  //   27 11 28 11 12 25 12 10 3f 28 10 12 28 24 12 10 60 84 3f 28 26 31 25 10 12 13 24 12 27 10 3e 28 10
  //   11 13 11 10 30 25 3f 28 10 12 13 28 13 24 12 10 3d 28 10 27 11 13 11 10 3e 28 10 12 13 28 13 24 12
  //   27 10 3f 28 10 12 13 28 12 11 13 11 10 3d 28 10 12 13 24 12 27 10 3e 28 10 12 13 28 12 11 13 11 10
  //   3f 28 26 31 25 10 12 13 24 12 27 11 13 11 10 50 13 40 17 40 97
endmodule

module _1bit_ALU (
  input  Sub,
  input  Cin,
  input  [3:0] Sel,
  input  A,
  input  B,
  input  Less,
  output Result,
  output Cout,
  output Set
);

  wire and_1_out, nor_1_out, or_1_out, xor_1_out, xor_2_out;

  and and_1 (and_1_out, A, B);
  or or_1 (or_1_out, A, B);
  nor nor_1 (nor_1_out, A, B);
  xor xor_1 (xor_1_out, A, B);
  Adder #(.width(1)) adder_1 (.a(A), .b(xor_2_out), .out(Set), .cin(Cin), .cout(Cout));
  xor xor_2 (xor_2_out, B, Sub);
  Multiplexer #(.select(4), .enable("false")) multiplexer_1 (
    .in0(and_1_out), .in1(or_1_out), .in2(nor_1_out), .in3(xor_1_out), .in4(Set), .in5(Less), .in15(Set),
    .out(Result), .sel(Sel));  // open: in6, in7, in8, in9, in10, in11, in12, in13, in14
endmodule

module _4bit_ALU (
  input  [3:0] Op,
  input  [3:0] A,
  input  [3:0] B,
  output [3:0] Result,
  output Zero,
  output Carry
);

  wire and_1_out, n1bit_alu_1_cout, n1bit_alu_2_cout, n1bit_alu_3_cout, n1bit_alu_4_cout, n1bit_alu_4_set,
       not_1_out;

  and and_1 (and_1_out, Op[0], Op[1], Op[2], Op[3]);
  _1bit_ALU u_1bit_alu_1 (
    .A(A[0]), .B(B[0]), .Less(n1bit_alu_4_set), .Result(Result[0]), .Sub(and_1_out), .Cin(and_1_out),
    .Sel(Op), .Cout(n1bit_alu_1_cout));  // open: Set
  _1bit_ALU u_1bit_alu_2 (
    .A(A[1]), .B(B[1]), .Less(1'b0), .Result(Result[1]), .Sub(and_1_out), .Cin(n1bit_alu_1_cout), .Sel(Op),
    .Cout(n1bit_alu_2_cout));  // open: Set
  _1bit_ALU u_1bit_alu_3 (
    .A(A[2]), .B(B[2]), .Less(1'b0), .Result(Result[2]), .Sub(and_1_out), .Cin(n1bit_alu_2_cout), .Sel(Op),
    .Cout(n1bit_alu_3_cout));  // open: Set
  _1bit_ALU u_1bit_alu_4 (
    .A(A[3]), .B(B[3]), .Less(1'b0), .Result(Result[3]), .Sub(and_1_out), .Cin(n1bit_alu_3_cout), .Sel(Op),
    .Cout(n1bit_alu_4_cout), .Set(n1bit_alu_4_set));
  nor nor_1 (Zero, Result[3], Result[2], Result[1], Result[0]);
  not not_1 (not_1_out, Zero);
  and and_2 (Carry, not_1_out, n1bit_alu_4_cout);
endmodule

module DECODER (
  input  [3:0] INSTRUCTION,
  input  II_P_CLOCK,
  input  I_P_CLOCK,
  input  ZERO_FLAG,
  input  CARRY_FLAG,
  input  [3:0] DATA,
  output PROGRAM_ADDRESS_REGISTER_E_WRITE,
  output PROGRAM_ADDRESS_REGISTER_D_WRITE,
  output PROGRAM_COUNTER_BUS_II_TOGGLE,
  output PROGRAM_COUNTER_BUS_I_TOGGLE,
  output PROGRAM_COUNTER_WRITE,
  output PROGRAM_ADDRESS_REGISTER_C_WRITE,
  output PROGRAM_ADDRESS_REGISTER_B_WRITE,
  output PROGRAM_ADDRESS_REGISTER_A_WRITE,
  output ROM_DATA_REGISTER_WRITE,
  output ALU_B_REGISTER_WRITE,
  output ALU_A_REGISTER_WRITE,
  output ALU_OPERATION_REGISTER_WRITE,
  output ALU_RESULT_REGISTER_WRITE,
  output RAM_ADDRESS_REGISTER_WRITE,
  output SELECT_RAM,
  output TOGGLE_RAM_WRITE_READ,
  output TOGGLE_ROM_DATA_BUS_CONNECTION,
  output TOGGLE_ALU_RESULT_BUS_CONNECTION,
  output DATA_SWITCH
);

  wire and_1_out, and_2_out, and_3_out, and_4_out, and_5_out, and_6_out, and_7_out, and_8_out, and_9_out,
       and_22_out, and_23_out, and_24_out, and_26_out, and_27_out, and_28_out, and_29_out, buffer_1_out,
       d_ff_1_q, d_ff_2_q, d_ff_3_q, d_ff_4_q, d_ff_5_q, d_ff_6_q, d_ff_7_q, not_1_out, not_2_out, not_3_out,
       not_4_out, not_5_out, not_6_out, not_7_out, not_8_out, not_9_out, not_10_out, or_3_out;
  wire [3:0] multiplexer_1_out;

  or or_1 (PROGRAM_COUNTER_WRITE, PROGRAM_COUNTER_BUS_II_TOGGLE, PROGRAM_COUNTER_BUS_I_TOGGLE);
  or or_2 (PROGRAM_COUNTER_BUS_I_TOGGLE, and_1_out, and_2_out, and_3_out, and_4_out, and_9_out);
  and and_1 (and_1_out, and_5_out, ZERO_FLAG);
  and and_2 (and_2_out, and_6_out, not_1_out);
  not not_1 (not_1_out, ZERO_FLAG);
  and and_3 (and_3_out, and_7_out, CARRY_FLAG);
  and and_4 (and_4_out, and_8_out, not_2_out);
  not not_2 (not_2_out, CARRY_FLAG);
  and and_5 (and_5_out, and_24_out, DATA[3], not_5_out, not_4_out, DATA[0]);
  and and_6 (and_6_out, and_24_out, DATA[3], not_5_out, DATA[1], not_6_out);
  and and_7 (and_7_out, and_24_out, DATA[3], not_5_out, DATA[1], DATA[0]);
  and and_8 (and_8_out, and_24_out, DATA[3], DATA[2], not_4_out, not_6_out);
  and and_9 (and_9_out, and_24_out, not_3_out, not_5_out, not_4_out, not_6_out);
  and and_10 (PROGRAM_ADDRESS_REGISTER_C_WRITE, and_24_out, not_3_out, not_5_out, DATA[1], DATA[0]);
  and and_11 (PROGRAM_ADDRESS_REGISTER_B_WRITE, and_24_out, not_3_out, not_5_out, DATA[1], not_6_out);
  and and_12 (PROGRAM_ADDRESS_REGISTER_A_WRITE, and_24_out, not_3_out, not_5_out, not_4_out, DATA[0]);
  and and_13 (ALU_B_REGISTER_WRITE, and_24_out, not_3_out, DATA[2], not_4_out, DATA[0]);
  and and_14 (ALU_A_REGISTER_WRITE, and_24_out, not_3_out, DATA[2], not_4_out, not_6_out);
  and and_15 (ALU_OPERATION_REGISTER_WRITE, and_24_out, not_3_out, DATA[2], DATA[1], not_6_out);
  and and_16 (ALU_RESULT_REGISTER_WRITE, and_24_out, not_3_out, DATA[2], DATA[1], DATA[0]);
  and and_17 (RAM_ADDRESS_REGISTER_WRITE, and_24_out, DATA[3], not_5_out, not_4_out, not_6_out);
  and and_18 (SELECT_RAM, and_26_out, not_3_out, not_5_out, DATA[1], DATA[0]);
  and and_19 (TOGGLE_RAM_WRITE_READ, and_26_out, not_3_out, not_5_out, DATA[1], not_6_out);
  and and_20 (TOGGLE_ROM_DATA_BUS_CONNECTION, and_26_out, not_3_out, not_5_out, not_4_out, not_6_out);
  and and_21 (TOGGLE_ALU_RESULT_BUS_CONNECTION, and_26_out, not_3_out, not_5_out, not_4_out, DATA[0]);
  not not_3 (not_3_out, DATA[3]);
  not not_4 (not_4_out, DATA[1]);
  not not_5 (not_5_out, DATA[2]);
  not not_6 (not_6_out, DATA[0]);
  D_Flip_Flop d_ff_1 (.clk(I_P_CLOCK), .D(d_ff_2_q), .Q(d_ff_1_q));  // open: Qn, preset, en, reset
  D_Flip_Flop d_ff_2 (.clk(I_P_CLOCK), .D(and_23_out), .Q(d_ff_2_q));  // open: Qn, preset, en, reset
  D_Flip_Flop d_ff_3 (.clk(I_P_CLOCK), .D(and_22_out), .Q(d_ff_3_q));  // open: Qn, preset, en, reset
  D_Flip_Flop d_ff_4 (.clk(I_P_CLOCK), .D(d_ff_3_q), .Q(d_ff_4_q));  // open: Qn, preset, en, reset
  D_Flip_Flop d_ff_5 (.clk(I_P_CLOCK), .D(d_ff_6_q), .Q(d_ff_5_q));  // open: Qn, preset, en, reset
  D_Flip_Flop d_ff_6 (.clk(I_P_CLOCK), .D(and_27_out), .Q(d_ff_6_q));  // open: Qn, preset, en, reset
  and and_22 (and_22_out, and_28_out, ZERO_FLAG);
  or or_3 (or_3_out, d_ff_2_q, d_ff_1_q, d_ff_3_q, d_ff_4_q, d_ff_6_q, d_ff_5_q);
  and and_23 (and_23_out, and_29_out, CARRY_FLAG);
  or or_4 (PROGRAM_ADDRESS_REGISTER_D_WRITE, and_29_out, and_28_out, and_27_out);
  and and_24 (and_24_out, not_7_out, multiplexer_1_out[1], not_9_out, not_10_out);
  and and_25 (ROM_DATA_REGISTER_WRITE, multiplexer_1_out[0], multiplexer_1_out[1], not_9_out, not_10_out);
  and and_26 (and_26_out, multiplexer_1_out[0], not_8_out, not_9_out, not_10_out);
  and and_27 (and_27_out, not_7_out, not_8_out, multiplexer_1_out[2], not_10_out);
  and and_28 (and_28_out, multiplexer_1_out[0], not_8_out, multiplexer_1_out[2], not_10_out);
  and and_29 (and_29_out, not_7_out, multiplexer_1_out[1], multiplexer_1_out[2], not_10_out);
  nor nor_1 (DATA_SWITCH, and_26_out, and_24_out);
  not not_7 (not_7_out, multiplexer_1_out[0]);
  not not_8 (not_8_out, multiplexer_1_out[1]);
  not not_9 (not_9_out, multiplexer_1_out[2]);
  and and_30 (PROGRAM_COUNTER_BUS_II_TOGGLE, or_3_out, d_ff_7_q);
  D_Flip_Flop d_ff_7 (
    .clk(II_P_CLOCK), .D(PROGRAM_ADDRESS_REGISTER_E_WRITE), .Q(d_ff_7_q));  // open: Qn, preset, en, reset
  D_Flip_Flop d_ff_8 (
    .clk(I_P_CLOCK), .D(PROGRAM_ADDRESS_REGISTER_D_WRITE), .Q(PROGRAM_ADDRESS_REGISTER_E_WRITE));  // open: Qn, preset, en, reset
  Multiplexer #(.width(4), .disabled(0), .enable("false")) multiplexer_1 (
    .in0(INSTRUCTION), .in1(4'b0000), .out(multiplexer_1_out), .sel(buffer_1_out));
  not not_10 (not_10_out, multiplexer_1_out[3]);
  buf buffer_1 (buffer_1_out, PROGRAM_ADDRESS_REGISTER_E_WRITE);

  // Notes on the sheet:
  //   WRITE TO
  //   DIRECT JUMP
  //   WRITE TO ROM REGISTER
  //   TOGGLE BUS CONNECTION
  //   DIRECT JUMP ON ZERO FLAG
  //   DIRECT JUMP ON CARRY FLAG
endmodule
